// Logisim project MIPSmonocycle.circ as structural Verilog: 5 circuits, main circuit main
module main (
);

  wire clk, control_unit_1_wbreg, cU3B, cUHW, jmpE, not_1_out, not_2_out, rDM, rst, wDM;
  wire [1:0] jmpM;
  wire [3:0] bit_extender_2_out, bit_extender_3_out, bit_extender_4_out, bit_extender_5_out;
  wire [15:0] DM_data;
  wire [23:0] bit_extender_1_out, bit_extender_7_out;
  wire [25:0] adressJM;
  wire [31:0] adder_1_out, alu_1_r, multiplexer_1_out, multiplexer_2_out, multiplexer_3_out, PC, sgnExtImmd,
       vRs;
  wire [31:16] DM_data_2;
  wire [31:26] IM_data;

  Button button_1 (.out(rst));
  Clock clock_1 (.out(clk));
  Adder #(.width(32)) adder_1 (.a(PC), .b(sgnExtImmd), .out(adder_1_out), .cin(1'b1));  // open: cout
  Multiplexer #(.select(2), .width(32), .enable("false")) multiplexer_1 (
    .in0(vRs), .in1({PC[31:26], adressJM}), .in2(adder_1_out), .in3(PC), .out(multiplexer_1_out), .sel(jmpM));
  not not_1 (not_1_out, jmpE);
  Counter #(.width(32), .max('hffff), .behavior("old")) u_PC (
    .load(jmpE), .D(multiplexer_1_out), .count(not_1_out), .Q(PC), .clk(clk), .clr(rst), .preset(1'b0));  // open: carry
  Bit_Extender #(.in_width(32), .out_width(24), .\type ("zero")) bit_extender_1 (.in(PC), .out(bit_extender_1_out));
  ROM #(.addrWidth(24), .dataWidth(32), .Select("low")) IM (
    .addr(bit_extender_1_out), .data({IM_data, adressJM}), .sel(1'b0));
  Bit_Extender #(.in_width(6), .out_width(4), .\type ("zero")) bit_extender_2 (.in(IM_data), .out(bit_extender_2_out));
  Bit_Extender #(.in_width(5), .out_width(4), .\type ("zero")) bit_extender_3 (
    .in(adressJM[20:16]), .out(bit_extender_3_out));
  Bit_Extender #(.in_width(5), .out_width(4), .\type ("zero")) bit_extender_4 (
    .in(adressJM[25:21]), .out(bit_extender_4_out));
  Bit_Extender #(.in_width(16), .out_width(4), .\type ("zero")) bit_extender_5 (
    .in(adressJM[15:0]), .out(bit_extender_5_out));
  // Probe on adressJM[25:21]
  assign sgnExtImmd = {{16{adressJM[15]}}, adressJM[15:0]};  // Bit_Extender bit_extender_6
  Control_Unit control_unit_1 (
    .opCode(IM_data), .wBREG(control_unit_1_wbreg), .clk(clk), .rst(rst), .jmpE(jmpE), .jmpM(jmpM),
    .funct(adressJM[5:0]), .wDM(wDM), .rDM(rDM), .cUHW(cUHW), .cU3B(cU3B));
  BREG breg_1 (
    .source_1(adressJM[25:21]), .target(adressJM[20:16]), .source_2(adressJM[20:16]),
    .\input (multiplexer_2_out), .clk(clk), .value_1(vRs), .w(control_unit_1_wbreg), .rst(rst));  // open: value_2
  Multiplexer #(.width(32), .disabled(0), .enable("false")) multiplexer_2 (
    .in0(multiplexer_3_out), .in1(alu_1_r), .out(multiplexer_2_out), .sel(not_2_out));
  not not_2 (not_2_out, rDM);
  Hex_Digit_Display hex_digit_display_1 (.value(bit_extender_2_out));  // open: dp
  Hex_Digit_Display hex_digit_display_2 (.value(bit_extender_4_out));  // open: dp
  Hex_Digit_Display hex_digit_display_3 (.value(bit_extender_3_out));  // open: dp
  ALU alu_1 (.A(vRs), .B(sgnExtImmd), .R(alu_1_r), .\function (adressJM[5:0]));
  Hex_Digit_Display hex_digit_display_4 (.value(bit_extender_5_out));  // open: dp
  Bit_Extender #(.in_width(32), .out_width(24), .\type ("zero")) bit_extender_7 (
    .in(alu_1_r), .out(bit_extender_7_out));
  Multiplexer #(.select(2), .width(32), .enable("false")) multiplexer_3 (
    .in0({DM_data_2, DM_data}), .in1({{16{1'b0}}, DM_data}), .in2({{24{1'b0}}, DM_data[7:0]}),
    .out(multiplexer_3_out), .sel({cU3B, cUHW}));  // open: in3
  RAM #(.addrWidth(24), .dataWidth(32), .bus("separate"), .Select("low")) DM (
    .addr(bit_extender_7_out), .data({DM_data_2, DM_data}), .str(wDM), .sel(1'b0), .clk(clk), .clr(rst));  // open: din, ld

  // Other names for the same wires on the sheet: funct[5:0] = adressJM[5:0]; shamt[4:0] = adressJM[10:6]

  // Notes on the sheet:
  //   Jump Register
  //   Jump
  //        Branch's$(Relative Jumps)
  //   Invalid Jump
  //   contents of IM (hex, n*v repeats v):
  //   0 20e50011 20e50010 0 a00008 9*0 e5001120
  //   opCode
  //   rs
  //   rt
  //   rd
  //   shamt
  //   funct
  //   immediate
endmodule

module ALU (
  input  [5:0] \function ,
  input  [31:0] A,
  input  [31:0] B,
  output [31:0] R
);

  Adder #(.width(32)) adder_1 (.a(A), .b(B), .out(R), .cin(1'b0));  // open: cout
endmodule

module register (
  input  D,
  output Q
);

  wire [31:1] register_1_q;

  Register #(.width(32), .trigger("high"), .Select("high")) register_1 (
    .Q({register_1_q, Q}), .cs(D));  // open: D, en, clk, clr, preset
  // Pins of 1 and 32 bits meet at {register_1_q, Q}
endmodule

module BREG (
  input  clk,
  input  rst,
  input  [31:0] \input ,
  input  [4:0] source_1,
  input  w,
  input  [4:0] target,
  input  [4:0] source_2,
  output [31:0] value_1,
  output [31:0] value_2
);

  wire decoder_1_out0, decoder_1_out1, decoder_1_out2, decoder_1_out3, decoder_1_out4, decoder_1_out5,
       decoder_1_out6, decoder_1_out7, decoder_1_out8, decoder_1_out9, decoder_1_out10, decoder_1_out11,
       decoder_1_out12, decoder_1_out13, decoder_1_out14, decoder_1_out15, decoder_1_out16, decoder_1_out17,
       decoder_1_out18, decoder_1_out19, decoder_1_out20, decoder_1_out21, decoder_1_out22, decoder_1_out23,
       decoder_1_out24, decoder_1_out25, decoder_1_out26, decoder_1_out27, decoder_1_out28, decoder_1_out29,
       decoder_1_out30, decoder_1_out31;
  wire [31:0] Q1, Q2, Q3, Q4, Q5, Q6, Q7, Q8, Q9, Q10, Q11, Q12, Q13, Q14, Q15, Q16, Q17, Q18, Q19, Q20, Q21,
       Q22, Q23, Q24, Q25, Q26, Q27, Q28, Q29, Q30, Q31;

  Decoder #(.select(5), .disabled(0)) decoder_1 (
    .out0(decoder_1_out0), .out1(decoder_1_out1), .out2(decoder_1_out2), .out3(decoder_1_out3),
    .out4(decoder_1_out4), .out5(decoder_1_out5), .out6(decoder_1_out6), .out7(decoder_1_out7),
    .out8(decoder_1_out8), .out9(decoder_1_out9), .out10(decoder_1_out10), .out11(decoder_1_out11),
    .out12(decoder_1_out12), .out13(decoder_1_out13), .out14(decoder_1_out14), .out15(decoder_1_out15),
    .out16(decoder_1_out16), .out17(decoder_1_out17), .out18(decoder_1_out18), .out19(decoder_1_out19),
    .out20(decoder_1_out20), .out21(decoder_1_out21), .out22(decoder_1_out22), .out23(decoder_1_out23),
    .out24(decoder_1_out24), .out25(decoder_1_out25), .out26(decoder_1_out26), .out27(decoder_1_out27),
    .out28(decoder_1_out28), .out29(decoder_1_out29), .out30(decoder_1_out30), .out31(decoder_1_out31),
    .sel(target), .en(w));
  Register #(.width(32), .Select("high")) R1 (
    .D(\input ), .en(decoder_1_out1), .Q(Q1), .clk(clk), .clr(rst), .cs(1'b1), .preset(1'b0));
  Register #(.width(32), .Select("high")) R2 (
    .D(\input ), .en(decoder_1_out2), .Q(Q2), .clk(clk), .clr(rst), .cs(1'b1), .preset(1'b0));
  Register #(.width(32), .Select("high")) R3 (
    .D(\input ), .en(decoder_1_out3), .Q(Q3), .clk(clk), .clr(rst), .cs(1'b1), .preset(1'b0));
  Register #(.width(32), .Select("high")) R28 (
    .D(\input ), .en(decoder_1_out28), .Q(Q28), .clk(clk), .clr(rst), .cs(1'b1), .preset(1'b0));
  Register #(.width(32), .Select("high")) R29 (
    .D(\input ), .en(decoder_1_out29), .Q(Q29), .clk(clk), .clr(rst), .cs(1'b1), .preset(1'b0));
  Register #(.width(32), .Select("high")) R30 (
    .D(\input ), .en(decoder_1_out30), .Q(Q30), .clk(clk), .clr(rst), .cs(1'b1), .preset(1'b0));
  Register #(.width(32), .Select("high")) R31 (
    .D(\input ), .en(decoder_1_out31), .Q(Q31), .clk(clk), .clr(rst), .cs(1'b1), .preset(1'b0));
  Register #(.width(32), .Select("high")) R4 (
    .D(\input ), .en(decoder_1_out4), .Q(Q4), .clk(clk), .clr(rst), .cs(1'b1), .preset(1'b0));
  Register #(.width(32), .Select("high")) R5 (
    .D(\input ), .en(decoder_1_out5), .Q(Q5), .clk(clk), .clr(rst), .cs(1'b1), .preset(1'b0));
  Register #(.width(32), .Select("high")) R6 (
    .D(\input ), .en(decoder_1_out6), .Q(Q6), .clk(clk), .clr(rst), .cs(1'b1), .preset(1'b0));
  Register #(.width(32), .Select("high")) R7 (
    .D(\input ), .en(decoder_1_out7), .Q(Q7), .clk(clk), .clr(rst), .cs(1'b1), .preset(1'b0));
  Register #(.width(32), .Select("high")) R24 (
    .D(\input ), .en(decoder_1_out24), .Q(Q24), .clk(clk), .clr(rst), .cs(1'b1), .preset(1'b0));
  Register #(.width(32), .Select("high")) R25 (
    .D(\input ), .en(decoder_1_out25), .Q(Q25), .clk(clk), .clr(rst), .cs(1'b1), .preset(1'b0));
  Register #(.width(32), .Select("high")) R26 (
    .D(\input ), .en(decoder_1_out26), .Q(Q26), .clk(clk), .clr(rst), .cs(1'b1), .preset(1'b0));
  Register #(.width(32), .Select("high")) R27 (
    .D(\input ), .en(decoder_1_out27), .Q(Q27), .clk(clk), .clr(rst), .cs(1'b1), .preset(1'b0));
  Register #(.width(32), .Select("high")) R8 (
    .D(\input ), .en(decoder_1_out8), .Q(Q8), .clk(clk), .clr(rst), .cs(1'b1), .preset(1'b0));
  Register #(.width(32), .Select("high")) R9 (
    .D(\input ), .en(decoder_1_out9), .Q(Q9), .clk(clk), .clr(rst), .cs(1'b1), .preset(1'b0));
  Register #(.width(32), .Select("high")) R10 (
    .D(\input ), .en(decoder_1_out10), .Q(Q10), .clk(clk), .clr(rst), .cs(1'b1), .preset(1'b0));
  Register #(.width(32), .Select("high")) R11 (
    .D(\input ), .en(decoder_1_out11), .Q(Q11), .clk(clk), .clr(rst), .cs(1'b1), .preset(1'b0));
  Register #(.width(32), .Select("high")) R20 (
    .D(\input ), .en(decoder_1_out20), .Q(Q20), .clk(clk), .clr(rst), .cs(1'b1), .preset(1'b0));
  Register #(.width(32), .Select("high")) R21 (
    .D(\input ), .en(decoder_1_out21), .Q(Q21), .clk(clk), .clr(rst), .cs(1'b1), .preset(1'b0));
  Register #(.width(32), .Select("high")) R22 (
    .D(\input ), .en(decoder_1_out22), .Q(Q22), .clk(clk), .clr(rst), .cs(1'b1), .preset(1'b0));
  Register #(.width(32), .Select("high")) R23 (
    .D(\input ), .en(decoder_1_out23), .Q(Q23), .clk(clk), .clr(rst), .cs(1'b1), .preset(1'b0));
  Register #(.width(32), .Select("high")) R12 (
    .D(\input ), .en(decoder_1_out12), .Q(Q12), .clk(clk), .clr(rst), .cs(1'b1), .preset(1'b0));
  Register #(.width(32), .Select("high")) R13 (
    .D(\input ), .en(decoder_1_out13), .Q(Q13), .clk(clk), .clr(rst), .cs(1'b1), .preset(1'b0));
  Register #(.width(32), .Select("high")) R14 (
    .D(\input ), .en(decoder_1_out14), .Q(Q14), .clk(clk), .clr(rst), .cs(1'b1), .preset(1'b0));
  Register #(.width(32), .Select("high")) R15 (
    .D(\input ), .en(decoder_1_out15), .Q(Q15), .clk(clk), .clr(rst), .cs(1'b1), .preset(1'b0));
  Register #(.width(32), .Select("high")) R16 (
    .D(\input ), .en(decoder_1_out16), .Q(Q16), .clk(clk), .clr(rst), .cs(1'b1), .preset(1'b0));
  Register #(.width(32), .Select("high")) R17 (
    .D(\input ), .en(decoder_1_out17), .Q(Q17), .clk(clk), .clr(rst), .cs(1'b1), .preset(1'b0));
  Register #(.width(32), .Select("high")) R18 (
    .D(\input ), .en(decoder_1_out18), .Q(Q18), .clk(clk), .clr(rst), .cs(1'b1), .preset(1'b0));
  Register #(.width(32), .Select("high")) R19 (
    .D(\input ), .en(decoder_1_out19), .Q(Q19), .clk(clk), .clr(rst), .cs(1'b1), .preset(1'b0));
  Multiplexer #(.select(5), .width(32), .enable("false")) multiplexer_1 (
    .in0({32{1'b0}}), .in1(Q1), .in2(Q2), .in3(Q3), .in4(Q4), .in5(Q5), .in6(Q6), .in7(Q7), .in8(Q8),
    .in9(Q9), .in10(Q10), .in11(Q11), .in12(Q12), .in13(Q13), .in14(Q14), .in15(Q15), .in16(Q16), .in17(Q17),
    .in18(Q18), .in19(Q19), .in20(Q20), .in21(Q21), .in22(Q22), .in23(Q23), .in24(Q24), .in25(Q25),
    .in26(Q26), .in27(Q27), .in28(Q28), .in29(Q29), .in30(Q30), .in31(Q31), .out(value_1), .sel(source_1));
  Multiplexer #(.select(5), .width(32), .enable("false")) multiplexer_2 (
    .in0({32{1'b0}}), .in1(Q1), .in2(Q2), .in3(Q3), .in4(Q4), .in5(Q5), .in6(Q6), .in7(Q7), .in8(Q8),
    .in9(Q9), .in10(Q10), .in11(Q11), .in12(Q12), .in13(Q13), .in14(Q14), .in15(Q15), .in16(Q16), .in17(Q17),
    .in18(Q18), .in19(Q19), .in20(Q20), .in21(Q21), .in22(Q22), .in23(Q23), .in24(Q24), .in25(Q25),
    .in26(Q26), .in27(Q27), .in28(Q28), .in29(Q29), .in30(Q30), .in31(Q31), .out(value_2), .sel(source_2));

  // Other names for the same wires on the sheet: D[31:0] = \input 

  // Notes on the sheet:
  //   R0
endmodule

module Control_Unit (
  input  [5:0] funct,
  input  clk,
  input  rst,
  input  [5:0] opCode,
  output wBREG,
  output wDM,
  output rDM,
  output cUHW,
  output cU3B,
  output jmpE,
  output [1:0] jmpM
);

  wire comparator_1_eq, multiplexer_1_out, multiplexer_2_out, multiplexer_4_out, multiplexer_5_out,
       multiplexer_7_out, multiplexer_8_out, multiplexer_10_out, multiplexer_12_out, multiplexer_13_out,
       multiplexer_14_out, multiplexer_16_out, multiplexer_17_out, not_1_out;

  Comparator #(.width(6)) comparator_1 (.a(funct), .b(6'b001000), .eq(comparator_1_eq));  // open: gt, lt
  not not_1 (not_1_out, comparator_1_eq);
  Comparator #(.width(6)) comparator_2 (.a(opCode), .b(6'b000011), .gt(jmpM[1]));  // open: eq, lt
  Comparator #(.width(6)) comparator_3 (.a(opCode), .b({6{1'b0}}), .gt(jmpM[0]));  // open: eq, lt
  Multiplexer #(.select(5), .enable("false")) multiplexer_1 (
    .in0(not_1_out), .in1(1'b0), .in2(1'b0), .in3(1'b0), .in4(1'b0), .in5(1'b0), .in6(1'b0), .in7(1'b0),
    .in8(1'b1), .in9(1'b0), .in10(1'b0), .in11(1'b0), .in12(1'b0), .in13(1'b0), .in14(1'b0), .in15(1'b0),
    .in16(1'b0), .in17(1'b0), .in18(1'b0), .in19(1'b0), .in20(1'b0), .in21(1'b0), .in22(1'b0), .in23(1'b0),
    .in24(1'b1), .in25(1'b0), .in26(1'b0), .in27(1'b0), .in28(1'b0), .in29(1'b0), .in30(1'b0), .in31(1'b0),
    .out(multiplexer_1_out), .sel(opCode[4:0]));
  Multiplexer #(.select(5), .enable("false")) multiplexer_2 (
    .in0(1'b0), .in1(1'b0), .in2(1'b0), .in3(1'b0), .in4(1'b0), .in5(1'b0), .in6(1'b0), .in7(1'b0),
    .in8(1'b0), .in9(1'b0), .in10(1'b0), .in11(1'b0), .in12(1'b0), .in13(1'b0), .in14(1'b0), .in15(1'b0),
    .in16(1'b0), .in17(1'b0), .in18(1'b0), .in19(1'b0), .in20(1'b0), .in21(1'b0), .in22(1'b0), .in23(1'b0),
    .in24(1'b0), .in25(1'b0), .in26(1'b0), .in27(1'b0), .in28(1'b0), .in29(1'b0), .in30(1'b0), .in31(1'b0),
    .out(multiplexer_2_out), .sel(opCode[4:0]));
  Multiplexer #(.enable("false")) multiplexer_3 (
    .in0(multiplexer_1_out), .in1(multiplexer_2_out), .out(wBREG), .sel(opCode[5]));
  Multiplexer #(.select(5), .enable("false")) multiplexer_4 (
    .in0(1'b0), .in1(1'b0), .in2(1'b0), .in3(1'b0), .in4(1'b0), .in5(1'b0), .in6(1'b0), .in7(1'b0),
    .in8(1'b0), .in9(1'b0), .in10(1'b0), .in11(1'b0), .in12(1'b0), .in13(1'b0), .in14(1'b0), .in15(1'b0),
    .in16(1'b0), .in17(1'b0), .in18(1'b0), .in19(1'b0), .in20(1'b0), .in21(1'b0), .in22(1'b0), .in23(1'b0),
    .in24(1'b0), .in25(1'b0), .in26(1'b0), .in27(1'b0), .in28(1'b0), .in29(1'b0), .in30(1'b0), .in31(1'b0),
    .out(multiplexer_4_out), .sel(opCode[4:0]));
  Multiplexer #(.select(5), .enable("false")) multiplexer_5 (
    .in0(1'b0), .in1(1'b0), .in2(1'b0), .in3(1'b0), .in4(1'b0), .in5(1'b0), .in6(1'b0), .in7(1'b0),
    .in8(1'b0), .in9(1'b0), .in10(1'b0), .in11(1'b0), .in12(1'b0), .in13(1'b0), .in14(1'b0), .in15(1'b0),
    .in16(1'b0), .in17(1'b0), .in18(1'b0), .in19(1'b0), .in20(1'b0), .in21(1'b0), .in22(1'b0), .in23(1'b0),
    .in24(1'b0), .in25(1'b0), .in26(1'b0), .in27(1'b0), .in28(1'b0), .in29(1'b0), .in30(1'b0), .in31(1'b0),
    .out(multiplexer_5_out), .sel(opCode[4:0]));
  Multiplexer #(.enable("false")) multiplexer_6 (
    .in0(multiplexer_4_out), .in1(multiplexer_5_out), .out(wDM), .sel(opCode[5]));
  Multiplexer #(.select(5), .enable("false")) multiplexer_7 (
    .in0(1'b0), .in1(1'b0), .in2(1'b0), .in3(1'b0), .in4(1'b0), .in5(1'b0), .in6(1'b0), .in7(1'b0),
    .in8(1'b0), .in9(1'b0), .in10(1'b0), .in11(1'b0), .in12(1'b0), .in13(1'b0), .in14(1'b0), .in15(1'b0),
    .in16(1'b0), .in17(1'b0), .in18(1'b0), .in19(1'b0), .in20(1'b0), .in21(1'b0), .in22(1'b0), .in23(1'b0),
    .in24(1'b1), .in25(1'b0), .in26(1'b0), .in27(1'b0), .in28(1'b0), .in29(1'b0), .in30(1'b0), .in31(1'b0),
    .out(multiplexer_7_out), .sel(opCode[4:0]));
  Multiplexer #(.select(5), .enable("false")) multiplexer_8 (
    .in0(1'b0), .in1(1'b0), .in2(1'b0), .in3(1'b0), .in4(1'b0), .in5(1'b0), .in6(1'b0), .in7(1'b0),
    .in8(1'b0), .in9(1'b0), .in10(1'b0), .in11(1'b0), .in12(1'b0), .in13(1'b0), .in14(1'b0), .in15(1'b0),
    .in16(1'b0), .in17(1'b0), .in18(1'b0), .in19(1'b0), .in20(1'b0), .in21(1'b0), .in22(1'b0), .in23(1'b0),
    .in24(1'b0), .in25(1'b0), .in26(1'b0), .in27(1'b0), .in28(1'b0), .in29(1'b0), .in30(1'b0), .in31(1'b0),
    .out(multiplexer_8_out), .sel(opCode[4:0]));
  Multiplexer #(.enable("false")) multiplexer_9 (
    .in0(multiplexer_7_out), .in1(multiplexer_8_out), .out(rDM), .sel(opCode[5]));
  Multiplexer #(.select(5), .enable("false")) multiplexer_10 (
    .in0(1'b0), .in1(1'b0), .in2(1'b0), .in3(1'b0), .in4(1'b0), .in5(1'b0), .in6(1'b0), .in7(1'b0),
    .in8(1'b0), .in9(1'b0), .in10(1'b0), .in11(1'b0), .in12(1'b0), .in13(1'b0), .in14(1'b0), .in15(1'b0),
    .in16(1'b0), .in17(1'b0), .in18(1'b0), .in19(1'b0), .in20(1'b0), .in21(1'b0), .in22(1'b0), .in23(1'b0),
    .in24(1'b1), .in25(1'b0), .in26(1'b0), .in27(1'b0), .in28(1'b0), .in29(1'b0), .in30(1'b0), .in31(1'b0),
    .out(multiplexer_10_out), .sel(opCode[4:0]));
  Multiplexer #(.enable("false")) multiplexer_11 (
    .in0(multiplexer_10_out), .in1(multiplexer_12_out), .out(cUHW), .sel(opCode[5]));
  Multiplexer #(.select(5), .enable("false")) multiplexer_12 (
    .in0(1'b0), .in1(1'b0), .in2(1'b0), .in3(1'b0), .in4(1'b0), .in5(1'b0), .in6(1'b0), .in7(1'b0),
    .in8(1'b0), .in9(1'b0), .in10(1'b0), .in11(1'b0), .in12(1'b0), .in13(1'b0), .in14(1'b0), .in15(1'b0),
    .in16(1'b0), .in17(1'b0), .in18(1'b0), .in19(1'b0), .in20(1'b0), .in21(1'b0), .in22(1'b0), .in23(1'b0),
    .in24(1'b0), .in25(1'b0), .in26(1'b0), .in27(1'b0), .in28(1'b0), .in29(1'b0), .in30(1'b0), .in31(1'b0),
    .out(multiplexer_12_out), .sel(opCode[4:0]));
  Multiplexer #(.select(5), .enable("false")) multiplexer_13 (
    .in0(1'b0), .in1(1'b0), .in2(1'b0), .in3(1'b0), .in4(1'b0), .in5(1'b0), .in6(1'b0), .in7(1'b0),
    .in8(1'b0), .in9(1'b0), .in10(1'b0), .in11(1'b0), .in12(1'b0), .in13(1'b0), .in14(1'b0), .in15(1'b0),
    .in16(1'b0), .in17(1'b0), .in18(1'b0), .in19(1'b0), .in20(1'b0), .in21(1'b0), .in22(1'b0), .in23(1'b0),
    .in24(1'b1), .in25(1'b0), .in26(1'b0), .in27(1'b0), .in28(1'b0), .in29(1'b0), .in30(1'b0), .in31(1'b0),
    .out(multiplexer_13_out), .sel(opCode[4:0]));
  Multiplexer #(.select(5), .enable("false")) multiplexer_14 (
    .in0(1'b0), .in1(1'b0), .in2(1'b0), .in3(1'b0), .in4(1'b0), .in5(1'b0), .in6(1'b0), .in7(1'b0),
    .in8(1'b0), .in9(1'b0), .in10(1'b0), .in11(1'b0), .in12(1'b0), .in13(1'b0), .in14(1'b0), .in15(1'b0),
    .in16(1'b0), .in17(1'b0), .in18(1'b0), .in19(1'b0), .in20(1'b0), .in21(1'b0), .in22(1'b0), .in23(1'b0),
    .in24(1'b0), .in25(1'b0), .in26(1'b0), .in27(1'b0), .in28(1'b0), .in29(1'b0), .in30(1'b0), .in31(1'b0),
    .out(multiplexer_14_out), .sel(opCode[4:0]));
  Multiplexer #(.enable("false")) multiplexer_15 (
    .in0(multiplexer_13_out), .in1(multiplexer_14_out), .out(cU3B), .sel(opCode[5]));
  Multiplexer #(.select(5), .enable("false")) multiplexer_16 (
    .in0(comparator_1_eq), .in1(1'b0), .in2(1'b0), .in3(1'b0), .in4(1'b0), .in5(1'b0), .in6(1'b0),
    .in7(1'b0), .in8(1'b0), .in9(1'b0), .in10(1'b0), .in11(1'b0), .in12(1'b0), .in13(1'b0), .in14(1'b0),
    .in15(1'b0), .in16(1'b0), .in17(1'b0), .in18(1'b0), .in19(1'b0), .in20(1'b0), .in21(1'b0), .in22(1'b0),
    .in23(1'b0), .in24(1'b0), .in25(1'b0), .in26(1'b0), .in27(1'b0), .in28(1'b0), .in29(1'b0), .in30(1'b0),
    .in31(1'b0), .out(multiplexer_16_out), .sel(opCode[4:0]));
  Multiplexer #(.select(5), .enable("false")) multiplexer_17 (
    .in0(1'b0), .in1(1'b0), .in2(1'b0), .in3(1'b0), .in4(1'b0), .in5(1'b0), .in6(1'b0), .in7(1'b0),
    .in8(1'b0), .in9(1'b0), .in10(1'b0), .in11(1'b0), .in12(1'b0), .in13(1'b0), .in14(1'b0), .in15(1'b0),
    .in16(1'b0), .in17(1'b0), .in18(1'b0), .in19(1'b0), .in20(1'b0), .in21(1'b0), .in22(1'b0), .in23(1'b0),
    .in24(1'b0), .in25(1'b0), .in26(1'b0), .in27(1'b0), .in28(1'b0), .in29(1'b0), .in30(1'b0), .in31(1'b0),
    .out(multiplexer_17_out), .sel(opCode[4:0]));
  Multiplexer #(.enable("false")) multiplexer_18 (
    .in0(multiplexer_16_out), .in1(multiplexer_17_out), .out(jmpE), .sel(opCode[5]));

  // Notes on the sheet:
  //   wBREG:
  //         Write sign to BREG
  //   jmpM:
  //         Jump Mode sign
  //   ADDI
  //   LBU
  //         Write sign to Data Memory
  //   wDM:
  //   ADDI
  //   LBU
  //   rDM:
  //         Read from Data $Memory to BREG sign
  //   ADDI
  //   LBU
  //   cUHW:
  //   Clear Upper Half-Word $sign on data to BREG load
  //   ADDI
  //   LBU
  //   cU3B:
  //   Clear Upper 3 Bytes on$data to BREG load
  //   ADDI
  //   LBU
  //   jmpE:
  //         Jump Enable sign
endmodule
